// Logisim project TrabalhoAp1_2.circ as structural Verilog: 1 circuit, main circuit main
module main (
  input  x,
  input  y,
  input  z,
  input  S0,
  input  S1,
  input  S2
);

  wire and_1_out, and_2_out, multiplexer_1_out, nand_1_out, nor_1_out, not_1_out, or_1_out, or_2_out;

  LED led_1 (.in(S0));
  LED led_2 (.in(S1));
  LED led_3 (.in(S2));
  or or_1 (or_1_out, x, y);
  not not_1 (not_1_out, z);
  and and_1 (and_1_out, S0, S1);
  or or_2 (or_2_out, S2, and_1_out);
  LED led_4 (.in(or_2_out));
  and and_2 (and_2_out, or_1_out, not_1_out);
  nand nand_1 (nand_1_out, x, y, z);
  nor nor_1 (nor_1_out, x, y, z);
  Multiplexer #(.select(3)) multiplexer_1 (
    .in0(and_2_out), .in1(nand_1_out), .in2(nor_1_out), .in3(1'b0), .in4(1'b0), .in5(1'b0), .in6(1'b0),
    .in7(1'b0), .out(multiplexer_1_out), .sel({S2, S1, S0}));  // open: en
  LED led_5 (.in(multiplexer_1_out));

  // Notes on the sheet:
  //   FUNCAO 2
  //   FUNCAO 3
  //   FUNCAO 1
  //   BUZZER
endmodule
