// Logisim project trabalhoap1_1.circ as structural Verilog: 1 circuit, main circuit main
module main (
  input  [2:0] in_1
);

  wire and_1_out, and_2_out, and_3_out, F2_out, F3_out, multiplexer_1_out, not_1_out, or_1_out, or_2_out,
       or_3_out, S0_out, S1_out, S2_out, X_out, Y_out;

  Button X (.out(X_out));
  Button Y (.out(Y_out));
  Button Z (.out(X_out));
  or or_1 (or_1_out, X_out, Y_out);
  LED led_1 (.in(S2_out));
  Button S2 (.out(S2_out));
  or F3 (F3_out, or_1_out, X_out);
  and and_1 (and_1_out, X_out, X_out, X_out, Y_out);
  or or_2 (or_2_out, X_out, Y_out);
  not not_1 (not_1_out, X_out);
  LED led_2 (.in(S1_out));
  Button S1 (.out(S1_out));
  and F2 (F2_out, and_1_out, X_out);
  LED led_3 (.in(S0_out));
  Button S0 (.out(S0_out));
  and and_2 (and_2_out, or_2_out, not_1_out);
  Multiplexer #(.select(3)) multiplexer_1 (
    .in0(and_2_out), .in1(F2_out), .in2(F3_out), .in3(1'b0), .in4(1'b0), .in5(1'b0), .in6(1'b0), .in7(1'b0),
    .out(multiplexer_1_out), .sel(in_1));  // open: en
  and and_3 (and_3_out, S0_out, S1_out);
  or or_3 (or_3_out, S2_out, and_3_out);
  LED led_4 (.in(multiplexer_1_out));
  LED led_5 (.in(or_3_out));

  // Notes on the sheet:
  //   F1
endmodule
