// Logisim project trabalhoap1_3.circ as structural Verilog: 5 circuits, main circuit main
module main (
  input  X,
  input  Y,
  input  Z,
  input  X_2,
  input  Y_2,
  input  Z_2,
  input  X_3,
  input  Y_3,
  input  [2:0] in_9,
  input  in_10,
  input  Z_3,
  input  in_12,
  input  in_13,
  input  in_14,
  input  in_15
);

  wire Buzzer_out_2, F1_out_4, F2_out_4, F3_out_4, multiplexer_1_out;

  F1 F1 (.X(X), .Y(Y), .Z(Z), .out_4(F1_out_4));
  F2 F2 (.in_1(X_2), .Y(Y_2), .Z(Z_2), .out_4(F2_out_4));
  F3 F3 (.X(X_3), .Y(Y_3), .Z(Z_3), .out_4(F3_out_4));
  Multiplexer #(.select(3)) multiplexer_1 (
    .in0(F1_out_4), .in1(F2_out_4), .in2(F3_out_4), .in3(in_10), .in4(in_12), .in5(in_13), .in6(in_14),
    .in7(in_15), .out(multiplexer_1_out), .sel(in_9));  // open: en
  LED led_1 (.in(multiplexer_1_out));
  Buzzer Buzzer (.in_1(in_9), .out_2(Buzzer_out_2));
  LED led_2 (.in(Buzzer_out_2));
endmodule

module F1 (
  input  X,
  input  Y,
  input  Z,
  output out_4
);

  wire not_1_out, or_1_out;

  not not_1 (not_1_out, Z);
  or or_1 (or_1_out, X, X, Y);
  and and_1 (out_4, or_1_out, not_1_out, not_1_out);
endmodule

module F2 (
  input  in_1,
  input  Y,
  input  Z,
  output out_4
);

  nand nand_1 (out_4, in_1, Y, Z);
endmodule

module F3 (
  input  X,
  input  Y,
  input  Z,
  output out_4
);

  nor nor_1 (out_4, X, X, Y, Z, Z);
endmodule

module Buzzer (
  input  [2:0] in_1,
  output out_2
);

  wire and_1_out;

  and and_1 (and_1_out, in_1[0], in_1[1]);
  or or_1 (out_2, and_1_out, in_1[2]);
endmodule
