// Logisim project trabalhoap1_Grupo4.circ as structural Verilog: 1 circuit, main circuit main
module main (
  input  in_1,
  input  F1,
  input  in_3,
  input  [2:0] Seletor
);

  wire and_1_out, multiplexer_1_out, nand_1_out, nor_1_out, or_1_out;

  or or_1 (or_1_out, in_1, F1);
  nand nand_1 (nand_1_out, in_1, F1, in_3);
  nor nor_1 (nor_1_out, in_1, F1, in_3);
  and and_1 (and_1_out, or_1_out, in_3);
  Multiplexer #(.select(3), .enable("false")) multiplexer_1 (
    .in0(and_1_out), .in1(nand_1_out), .in2(nor_1_out), .in3(1'b0), .in4(1'b0), .in5(1'b0), .in6(1'b0),
    .in7(1'b0), .out(multiplexer_1_out), .sel(Seletor));
  LED led_1 (.in(multiplexer_1_out));

  // Notes on the sheet:
  //   F2
  //   F3
  //   Ground
  //   000  -> F1
  //   001  -> F2
  //   010  -> F3
endmodule
